# Fritzing sketch speaker (saved by Fritzing 0.9.3b)
breadboards: 1

parts:
  Componente2 = Arduino Uno (Rev3)
  J1 = Piezo Speaker

nets:
  N1: Componente2.D9_PWM, J1.pin2
  N2: Componente2.AREF, J1.pin1
